// Logisim project All Gates For Design.circ as structural Verilog: 1 circuit, main circuit main
module main (
  input  A,
  input  A_2,
  input  A_3,
  input  B,
  input  B_2,
  input  A_4,
  input  A_5,
  input  A_6,
  input  B_3,
  input  B_4,
  input  B_5,
  output F,
  output A_prime,
  output F_2,
  output F_3,
  output F_4
);

  wire or_1_out;

  and and_1 (F, A, B);
  nand nand_1 (F_2, A_4, B_3);
  or or_1 (or_1_out, A_2, B_2);
  nor nor_1 (F_3, A_5, B_4);
  not not_1 (A_prime, A_3);
  xor xor_1 (F_4, A_6, B_5);

  // Notes on the sheet:
  //   AND GATE
  //   NAND GATE
  //   Circuit Diagram
  //   Experiment 1
  //   OR GATE
  //   NOR GATE
  //   F
  //   NOT GATE
  //   XOR GATE
endmodule
