// Logisim project Extension of inputs of AND and OR Gates.circ as structural Verilog: 1 circuit, main circuit main
module main (
  input  A,
  input  A_2,
  input  B,
  input  B_2,
  input  C,
  input  C_2,
  output F,
  output F_2
);

  wire and_1_out, or_1_out;

  and and_1 (and_1_out, A, B);
  and and_2 (F, and_1_out, C);
  or or_1 (or_1_out, A_2, B_2);
  or or_2 (F_2, or_1_out, C_2);

  // Notes on the sheet:
  //   Circuit Diagram
  //   Experiment 2
  //   Figure: Extension of inputs of AND and OR Gates
endmodule
