// Logisim project Logic Diagram for (F = A'C + AB' + BC) Boolean function.circ as structural Verilog: 1 circuit, main circuit main
module main (
  input  A,
  input  B,
  input  C,
  output out_4
);

  wire and_1_out, and_2_out, and_3_out, not_1_out, not_2_out, or_1_out;

  not not_1 (not_1_out, A);
  not not_2 (not_2_out, B);
  and and_1 (and_1_out, not_1_out, C);
  and and_2 (and_2_out, A, not_2_out);
  and and_3 (and_3_out, B, C);
  or or_1 (or_1_out, and_1_out, and_2_out);
  or or_2 (out_4, or_1_out, and_3_out);

  // Notes on the sheet:
  //   Circuit Diagram
  //   Experiment 3
  //   I1 = A'C
  //   I2 = AB'
  //   I3 = BC
  //   Figure: Logic Diagram for the given Boolean function
  //   I1 + I2 = A'C + AB'
  //   F = A'C + AB' + BC
endmodule
